// Logisim project sagui.circ as structural Verilog: 10 circuits, main circuit main
module register_bank (
  input  RC,
  input  [1:0] RA,
  input  [1:0] RB,
  input  [7:0] D,
  input  FWE,
  input  [1:0] FRD,
  input  WE,
  input  [1:0] RD,
  input  CLK,
  output [7:0] DB,
  output [7:0] DA,
  output BLK
);

  wire demultiplexer_1_out0, demultiplexer_1_out1, demultiplexer_1_out2, demultiplexer_1_out3,
       demultiplexer_2_out0, demultiplexer_2_out1, demultiplexer_2_out2, demultiplexer_2_out3,
       multiplexer_2_out, multiplexer_4_out, register_with_counter_1_blk, register_with_counter_2_blk,
       register_with_counter_3_blk, register_with_counter_4_blk;
  wire [7:0] register_with_counter_1_q, register_with_counter_2_q, register_with_counter_3_q,
       register_with_counter_4_q;

  Demultiplexer #(.select(2)) demultiplexer_1 (
    .out0(demultiplexer_1_out0), .out1(demultiplexer_1_out1), .out2(demultiplexer_1_out2),
    .out3(demultiplexer_1_out3), .in(FWE), .sel(FRD));
  Demultiplexer #(.select(2)) demultiplexer_2 (
    .out0(demultiplexer_2_out0), .out1(demultiplexer_2_out1), .out2(demultiplexer_2_out2),
    .out3(demultiplexer_2_out3), .in(WE), .sel(RD));
  Multiplexer #(.select(2), .width(8)) multiplexer_1 (
    .in0(register_with_counter_1_q), .in1(register_with_counter_2_q), .in2(register_with_counter_3_q),
    .in3(register_with_counter_4_q), .out(DA), .sel(RA));
  register_with_counter register_with_counter_1 (
    .D(D), .INC(demultiplexer_1_out0), .WE(demultiplexer_2_out0), .CLK(CLK), .RC(RC),
    .Q(register_with_counter_1_q), .BLK(register_with_counter_1_blk));
  register_with_counter register_with_counter_2 (
    .D(D), .INC(demultiplexer_1_out1), .WE(demultiplexer_2_out1), .CLK(CLK), .RC(RC),
    .Q(register_with_counter_2_q), .BLK(register_with_counter_2_blk));
  register_with_counter register_with_counter_3 (
    .D(D), .INC(demultiplexer_1_out2), .WE(demultiplexer_2_out2), .CLK(CLK), .RC(RC),
    .Q(register_with_counter_3_q), .BLK(register_with_counter_3_blk));
  register_with_counter register_with_counter_4 (
    .D(D), .INC(demultiplexer_1_out3), .WE(demultiplexer_2_out3), .CLK(CLK), .RC(RC),
    .Q(register_with_counter_4_q), .BLK(register_with_counter_4_blk));
  Multiplexer #(.select(2)) multiplexer_2 (
    .in0(register_with_counter_1_blk), .in1(register_with_counter_2_blk), .in2(register_with_counter_3_blk),
    .in3(register_with_counter_4_blk), .out(multiplexer_2_out), .sel(RA));
  or or_1 (BLK, multiplexer_2_out, multiplexer_4_out);
  Multiplexer #(.select(2), .width(8)) multiplexer_3 (
    .in0(register_with_counter_1_q), .in1(register_with_counter_2_q), .in2(register_with_counter_3_q),
    .in3(register_with_counter_4_q), .out(DB), .sel(RB));
  Multiplexer #(.select(2)) multiplexer_4 (
    .in0(register_with_counter_1_blk), .in1(register_with_counter_2_blk), .in2(register_with_counter_3_blk),
    .in3(register_with_counter_4_blk), .out(multiplexer_4_out), .sel(RB));
endmodule

module main (
);

  wire adder_1_cout, adder_2_cout, and_1_out, and_2_out, and_3_out, clock_1_out, idecoder_1_jmp,
       idecoder_1_jmpz, idecoder_1_mwe, idecoder_1_rwe, idecoder_1_useimm, not_1_out, or_1_out, or_2_out,
       or_3_out, pipe_dere_1_jmp_out, pipe_dere_1_jmpz_out, pipe_dere_1_mwe_out, pipe_dere_1_rwe_out,
       pipe_dere_1_useimm_out, pipe_exmd_1_branch_out, pipe_exmd_1_load_out, pipe_exmd_1_mwe_out,
       pipe_exmd_1_rwe_out, pipe_mdwb_1_load_out, pipe_mdwb_1_we_out, pipe_reex_1_jmp_out,
       pipe_reex_1_jmpz_out, pipe_reex_1_mwe_out, pipe_reex_1_rwe_out, pipe_reex_1_useimm_out,
       register_bank_1_blk, Reset_Pipeline_out;
  wire [1:0] multiplexer_2_out, multiplexer_3_out, pipe_exmd_1_rd_out, pipe_mdwb_1_rd_out, pipe_reex_1_rd_out;
  wire [3:0] pipe_dere_1_instr_out, pipe_dere_1_opcode_out, pipe_reex_1_opcode_out;
  wire [7:0] adder_1_out, adder_2_out, alu_1_r, bit_extender_1_out, MD_dout, MI_data, multiplexer_1_out,
       multiplexer_4_out, multiplexer_5_out, multiplexer_6_out, multiplexer_7_out, multiplexer_8_out, PC_q,
       pipe_dere_1_pc_out, pipe_exmd_1_da_out, pipe_exmd_1_pc_out, pipe_exmd_1_res_out, pipe_mdwb_1_mem_out,
       pipe_mdwb_1_res_out, pipe_mide_1_i_out, pipe_mide_1_pc_out, pipe_reex_1_da_out, pipe_reex_1_db_out,
       pipe_reex_1_imm_out, pipe_reex_1_pc_out, register_bank_1_da, register_bank_1_db;

  Adder adder_1 (.a(PC_q), .b(8'h1), .out(adder_1_out), .cin(1'b0), .cout(adder_1_cout));
  Multiplexer #(.width(8)) multiplexer_1 (
    .in0(adder_1_out), .in1(pipe_exmd_1_pc_out), .out(multiplexer_1_out), .sel(pipe_exmd_1_branch_out));
  not not_1 (not_1_out, register_bank_1_blk);
  LED led_1 (.in(adder_1_cout));
  Register PC (.D(multiplexer_1_out), .en(not_1_out), .clk(clock_1_out), .Q(PC_q), .clr(1'b0));
  ROM MI (.addr(PC_q), .data(MI_data));
  // Probe on MI_data
  PIPE_MIDE pipe_mide_1 (
    .I_in(MI_data), .R(or_1_out), .PC_in(PC_q), .Clk(and_1_out), .I_out(pipe_mide_1_i_out),
    .PC_out(pipe_mide_1_pc_out));
  or or_1 (or_1_out, Reset_Pipeline_out, pipe_exmd_1_branch_out);
  Button Reset_Pipeline (.out(Reset_Pipeline_out));
  and and_1 (and_1_out, clock_1_out, ~register_bank_1_blk);  // AND_Gate
  Clock clock_1 (.out(clock_1_out));
  idecoder idecoder_1 (
    .opcode(pipe_mide_1_i_out[7:4]), .jmpz(idecoder_1_jmpz), .jmp(idecoder_1_jmp),
    .useImm(idecoder_1_useimm), .RWE(idecoder_1_rwe), .MWE(idecoder_1_mwe));
  PIPE_DERE pipe_dere_1 (
    .Instr_in(pipe_mide_1_i_out[3:0]), .jmpz_in(idecoder_1_jmpz), .jmp_in(idecoder_1_jmp),
    .useImm_in(idecoder_1_useimm), .RWE_in(idecoder_1_rwe), .MWE_in(idecoder_1_mwe),
    .opcode_in(pipe_mide_1_i_out[7:4]), .PC_in(pipe_mide_1_pc_out), .Clk(and_1_out), .R(or_1_out),
    .Instr_out(pipe_dere_1_instr_out), .jmpz_out(pipe_dere_1_jmpz_out), .jmp_out(pipe_dere_1_jmp_out),
    .useImm_out(pipe_dere_1_useimm_out), .RWE_out(pipe_dere_1_rwe_out), .MWE_out(pipe_dere_1_mwe_out),
    .opcode_out(pipe_dere_1_opcode_out), .PC_out(pipe_dere_1_pc_out));
  Multiplexer #(.width(2)) multiplexer_2 (
    .in0(pipe_dere_1_instr_out[3:2]), .in1(2'b00), .out(multiplexer_2_out), .sel(pipe_dere_1_useimm_out));
  Multiplexer #(.width(2)) multiplexer_3 (
    .in0(pipe_dere_1_instr_out[1:0]), .in1(2'b00), .out(multiplexer_3_out), .sel(pipe_dere_1_useimm_out));
  assign bit_extender_1_out = {{4{pipe_dere_1_instr_out[3]}}, pipe_dere_1_instr_out};  // Bit_Extender bit_extender_1
  register_bank register_bank_1 (
    .RC(pipe_exmd_1_branch_out), .RA(multiplexer_2_out), .RB(multiplexer_3_out), .D(multiplexer_8_out),
    .FWE(pipe_dere_1_rwe_out), .FRD(multiplexer_2_out), .WE(pipe_mdwb_1_we_out), .RD(pipe_mdwb_1_rd_out),
    .CLK(clock_1_out), .DB(register_bank_1_db), .DA(register_bank_1_da), .BLK(register_bank_1_blk));
  or or_2 (or_2_out, or_1_out, register_bank_1_blk);
  Multiplexer #(.width(8)) multiplexer_4 (
    .in0(register_bank_1_da), .in1(register_bank_1_db), .out(multiplexer_4_out), .sel(pipe_dere_1_useimm_out));
  Multiplexer #(.width(8)) multiplexer_5 (
    .in0({8{1'b0}}), .in1(register_bank_1_db), .out(multiplexer_5_out), .sel(pipe_dere_1_useimm_out));
  PIPE_REEX pipe_reex_1 (
    .Imm_in(bit_extender_1_out), .DA_in(multiplexer_4_out), .DB_in(multiplexer_5_out),
    .jmpz_in(pipe_dere_1_jmpz_out), .jmp_in(pipe_dere_1_jmp_out), .useImm_in(pipe_dere_1_useimm_out),
    .RWE_in(pipe_dere_1_rwe_out), .MWE_in(pipe_dere_1_mwe_out), .opcode_in(pipe_dere_1_opcode_out),
    .PC_in(pipe_dere_1_pc_out), .RD_in(multiplexer_2_out), .Clk(clock_1_out), .R(or_2_out),
    .Imm_out(pipe_reex_1_imm_out), .DA_out(pipe_reex_1_da_out), .DB_out(pipe_reex_1_db_out),
    .jmpz_out(pipe_reex_1_jmpz_out), .jmp_out(pipe_reex_1_jmp_out), .useImm_out(pipe_reex_1_useimm_out),
    .RWE_out(pipe_reex_1_rwe_out), .MWE_out(pipe_reex_1_mwe_out), .opcode_out(pipe_reex_1_opcode_out),
    .PC_out(pipe_reex_1_pc_out), .RD_out(pipe_reex_1_rd_out));
  Adder adder_2 (.a(pipe_reex_1_pc_out), .b(pipe_reex_1_imm_out), .out(adder_2_out), .cin(1'b0), .cout(adder_2_cout));
  LED led_2 (.in(adder_2_cout));
  Multiplexer #(.width(8)) multiplexer_6 (
    .in0(pipe_reex_1_db_out), .in1(pipe_reex_1_imm_out), .out(multiplexer_6_out), .sel(pipe_reex_1_useimm_out));
  Multiplexer #(.width(8)) multiplexer_7 (
    .in0(pipe_reex_1_db_out), .in1(adder_2_out), .out(multiplexer_7_out), .sel(pipe_reex_1_useimm_out));
  and and_2 (and_2_out, ~pipe_reex_1_opcode_out[0], ~pipe_reex_1_opcode_out[1], pipe_reex_1_opcode_out[2], ~pipe_reex_1_opcode_out[3]);  // AND_Gate
  alu alu_1 (.A(pipe_reex_1_da_out), .B(multiplexer_6_out), .opcode(pipe_reex_1_opcode_out), .R(alu_1_r));
  or or_3 (or_3_out, pipe_reex_1_jmp_out, and_3_out);
  and and_3 (and_3_out, pipe_reex_1_jmpz_out, ~alu_1_r[0]);  // AND_Gate
  RAM MD (
    .addr(pipe_exmd_1_res_out), .we(pipe_exmd_1_mwe_out), .oe(1'b1), .clk(clock_1_out),
    .din(pipe_exmd_1_da_out), .dout(MD_dout));
  PIPE_EXMD pipe_exmd_1 (
    .DA_in(pipe_reex_1_da_out), .Branch_in(or_3_out), .Res_in(alu_1_r), .Load_in(and_2_out),
    .RWE_in(pipe_reex_1_rwe_out), .MWE_in(pipe_reex_1_mwe_out), .PC_in(multiplexer_7_out),
    .RD_in(pipe_reex_1_rd_out), .R(or_1_out), .Clk(clock_1_out), .DA_out(pipe_exmd_1_da_out),
    .Branch_out(pipe_exmd_1_branch_out), .Res_out(pipe_exmd_1_res_out), .Load_out(pipe_exmd_1_load_out),
    .RWE_out(pipe_exmd_1_rwe_out), .MWE_out(pipe_exmd_1_mwe_out), .PC_out(pipe_exmd_1_pc_out),
    .RD_out(pipe_exmd_1_rd_out));
  PIPE_MDWB pipe_mdwb_1 (
    .Res_in(pipe_exmd_1_res_out), .Mem_in(MD_dout), .Load_in(pipe_exmd_1_rwe_out),
    .RD_in(pipe_exmd_1_rd_out), .WE_in(pipe_exmd_1_load_out), .Clk(clock_1_out), .R(Reset_Pipeline_out),
    .Res_out(pipe_mdwb_1_res_out), .Mem_out(pipe_mdwb_1_mem_out), .Load_out(pipe_mdwb_1_load_out),
    .RD_out(pipe_mdwb_1_rd_out), .WE_out(pipe_mdwb_1_we_out));
  Multiplexer #(.width(8)) multiplexer_8 (
    .in0(pipe_mdwb_1_res_out), .in1(pipe_mdwb_1_mem_out), .out(multiplexer_8_out), .sel(pipe_mdwb_1_load_out));

  // Notes on the sheet:
  //   contents of MI (hex, n*v repeats v):
  //   85 64 a0 1 60 88 20 60 a0 12 60 81 13 0 32 60 a0 81 64 a0 7f 91 a1 c1 b1 d0 d0 64 e1 f1 8a 64 7f 54
  //   a5 44 8d 73 68 a0 8a 6c 8c 73 c a0 46 8a 98 42 94 56 a0 89 a8 81 ac 8a 72 20 60 1 2 3 4 5 6 7 8 9 a
  //   1 2 3 4 5 6 7 8 9 a
endmodule

module register_with_counter (
  input  [7:0] D,
  input  INC,
  input  WE,
  input  CLK,
  input  RC,
  output [7:0] Q,
  output BLK
);

  wire [1:0] C_q, multiplexer_1_out, multiplexer_2_out, multiplexer_3_out;

  Multiplexer #(.select(2), .width(2)) multiplexer_1 (
    .in0(2'b01), .in1(2'b10), .in2(2'b11), .in3(2'b11), .out(multiplexer_1_out), .sel(C_q));
  Multiplexer #(.select(2), .width(2)) multiplexer_2 (
    .in0(2'b00), .in1(2'b00), .in2(2'b01), .in3(2'b10), .out(multiplexer_2_out), .sel(C_q));
  Register R (.D(D), .en(WE), .clk(CLK), .Q(Q), .clr(1'b0));
  Register #(.width(2)) C (.D(multiplexer_3_out), .en(1'b1), .clk(CLK), .Q(C_q), .clr(RC));
  Multiplexer #(.select(2), .width(2)) multiplexer_3 (
    .in0(C_q), .in1(multiplexer_1_out), .in2(multiplexer_2_out), .in3(C_q), .out(multiplexer_3_out),
    .sel({WE, INC}));
  or or_1 (BLK, C_q[0], C_q[1]);
endmodule

module idecoder (
  input  [3:0] opcode,
  output jmpz,
  output jmp,
  output useImm,
  output RWE,
  output MWE
);

  wire and_1_out, and_2_out, and_3_out, and_4_out, and_7_out, or_1_out;

  and and_1 (and_1_out, opcode[0], ~opcode[3]);  // AND_Gate
  and and_2 (and_2_out, opcode[2], opcode[1]);
  or or_1 (or_1_out, and_2_out, ~opcode[2]);  // OR_Gate
  and and_3 (and_3_out, ~opcode[0], ~opcode[1], ~opcode[2], opcode[3]);  // AND_Gate
  and and_4 (and_4_out, or_1_out, and_1_out);
  and and_5 (jmp, ~opcode[3], ~opcode[2], opcode[1]);  // AND_Gate
  and and_6 (jmpz, ~opcode[3], ~opcode[2], ~opcode[1]);  // AND_Gate
  or or_2 (useImm, and_3_out, and_4_out);
  and and_7 (and_7_out, ~opcode[3], ~opcode[2]);  // AND_Gate
  and and_8 (MWE, ~opcode[3], opcode[2], ~opcode[1], opcode[0]);  // AND_Gate
  and and_9 (RWE, ~MWE, ~and_7_out);  // AND_Gate
endmodule

module PIPE_MIDE (
  input  [7:0] I_in,
  input  R,
  input  [7:0] PC_in,
  input  Clk,
  output [7:0] I_out,
  output [7:0] PC_out
);

  wire [7:0] multiplexer_1_out;

  Multiplexer #(.width(8)) multiplexer_1 (.in0(I_in), .in1(8'hf0), .out(multiplexer_1_out), .sel(R));
  Register Instr (.D(multiplexer_1_out), .en(1'b1), .clk(Clk), .Q(I_out), .clr(1'b0));
  Register PC (.D(PC_in), .en(1'b1), .clk(Clk), .Q(PC_out), .clr(1'b0));
endmodule

module PIPE_DERE (
  input  [3:0] Instr_in,
  input  jmpz_in,
  input  jmp_in,
  input  useImm_in,
  input  RWE_in,
  input  MWE_in,
  input  [3:0] opcode_in,
  input  [7:0] PC_in,
  input  Clk,
  input  R,
  output [3:0] Instr_out,
  output jmpz_out,
  output jmp_out,
  output useImm_out,
  output RWE_out,
  output MWE_out,
  output [3:0] opcode_out,
  output [7:0] PC_out
);

  wire multiplexer_2_out, multiplexer_3_out, multiplexer_4_out, multiplexer_5_out, multiplexer_6_out;
  wire [3:0] multiplexer_1_out, multiplexer_7_out;

  Multiplexer #(.width(4)) multiplexer_1 (.in0(Instr_in), .in1(4'b0000), .out(multiplexer_1_out), .sel(R));
  Multiplexer multiplexer_2 (.in0(jmpz_in), .in1(1'b0), .out(multiplexer_2_out), .sel(R));
  Multiplexer multiplexer_3 (.in0(jmp_in), .in1(1'b0), .out(multiplexer_3_out), .sel(R));
  Multiplexer multiplexer_4 (.in0(useImm_in), .in1(1'b0), .out(multiplexer_4_out), .sel(R));
  Multiplexer multiplexer_5 (.in0(RWE_in), .in1(1'b0), .out(multiplexer_5_out), .sel(R));
  Multiplexer multiplexer_6 (.in0(MWE_in), .in1(1'b0), .out(multiplexer_6_out), .sel(R));
  Multiplexer #(.width(4)) multiplexer_7 (.in0(opcode_in), .in1(4'b1111), .out(multiplexer_7_out), .sel(R));
  Register #(.width(4)) Instr (.D(multiplexer_1_out), .en(1'b1), .clk(Clk), .Q(Instr_out), .clr(1'b0));
  Register #(.width(1)) jmpz (.D(multiplexer_2_out), .en(1'b1), .clk(Clk), .Q(jmpz_out), .clr(1'b0));
  Register #(.width(1)) jmp (.D(multiplexer_3_out), .en(1'b1), .clk(Clk), .Q(jmp_out), .clr(1'b0));
  Register #(.width(1)) useImm (.D(multiplexer_4_out), .en(1'b1), .clk(Clk), .Q(useImm_out), .clr(1'b0));
  Register #(.width(1)) RWE (.D(multiplexer_5_out), .en(1'b1), .clk(Clk), .Q(RWE_out), .clr(1'b0));
  Register #(.width(1)) MWE (.D(multiplexer_6_out), .en(1'b1), .clk(Clk), .Q(MWE_out), .clr(1'b0));
  Register #(.width(4)) opcode (.D(multiplexer_7_out), .en(1'b1), .clk(Clk), .Q(opcode_out), .clr(1'b0));
  Register PC (.D(PC_in), .en(1'b1), .clk(Clk), .Q(PC_out), .clr(1'b0));
endmodule

module PIPE_REEX (
  input  [7:0] Imm_in,
  input  [7:0] DA_in,
  input  [7:0] DB_in,
  input  jmpz_in,
  input  jmp_in,
  input  useImm_in,
  input  RWE_in,
  input  MWE_in,
  input  [3:0] opcode_in,
  input  [7:0] PC_in,
  input  [1:0] RD_in,
  input  Clk,
  input  R,
  output [7:0] Imm_out,
  output [7:0] DA_out,
  output [7:0] DB_out,
  output jmpz_out,
  output jmp_out,
  output useImm_out,
  output RWE_out,
  output MWE_out,
  output [3:0] opcode_out,
  output [7:0] PC_out,
  output [1:0] RD_out
);

  wire multiplexer_1_out, multiplexer_2_out, multiplexer_3_out, multiplexer_4_out;
  wire [3:0] multiplexer_5_out;

  Register Imm (.D(Imm_in), .en(1'b1), .clk(Clk), .Q(Imm_out), .clr(1'b0));
  Register DA (.D(DA_in), .en(1'b1), .clk(Clk), .Q(DA_out), .clr(1'b0));
  Register DB (.D(DB_in), .en(1'b1), .clk(Clk), .Q(DB_out), .clr(1'b0));
  Register #(.width(1)) jmpz (.D(multiplexer_1_out), .en(1'b1), .clk(Clk), .Q(jmpz_out), .clr(1'b0));
  Multiplexer multiplexer_1 (.in0(jmpz_in), .in1(1'b0), .out(multiplexer_1_out), .sel(R));
  Register #(.width(1)) jmp (.D(multiplexer_2_out), .en(1'b1), .clk(Clk), .Q(jmp_out), .clr(1'b0));
  Multiplexer multiplexer_2 (.in0(jmp_in), .in1(1'b0), .out(multiplexer_2_out), .sel(R));
  Register #(.width(1)) useImm (.D(useImm_in), .en(1'b1), .clk(Clk), .Q(useImm_out), .clr(1'b0));
  Register #(.width(1)) RWE (.D(multiplexer_3_out), .en(1'b1), .clk(Clk), .Q(RWE_out), .clr(1'b0));
  Multiplexer multiplexer_3 (.in0(RWE_in), .in1(1'b0), .out(multiplexer_3_out), .sel(R));
  Register #(.width(1)) MWE (.D(multiplexer_4_out), .en(1'b1), .clk(Clk), .Q(MWE_out), .clr(1'b0));
  Multiplexer multiplexer_4 (.in0(MWE_in), .in1(1'b0), .out(multiplexer_4_out), .sel(R));
  Register #(.width(4)) opcode (.D(multiplexer_5_out), .en(1'b1), .clk(Clk), .Q(opcode_out), .clr(1'b0));
  Multiplexer #(.width(4)) multiplexer_5 (.in0(opcode_in), .in1(4'b1111), .out(multiplexer_5_out), .sel(R));
  Register PC (.D(PC_in), .en(1'b1), .clk(Clk), .Q(PC_out), .clr(1'b0));
  Register #(.width(2)) RD (.D(RD_in), .en(1'b1), .clk(Clk), .Q(RD_out), .clr(1'b0));
endmodule

module alu (
  input  [7:0] A,
  input  [7:0] B,
  input  [3:0] opcode,
  output [7:0] R
);

  wire adder_1_cout, or_1_out;
  wire [7:0] adder_1_out, and_1_out, bit_extender_1_out, multiplexer_1_out, negator_1_out, not_1_out,
       or_2_out, shifter_1_out, shifter_2_out;

  Negator negator_1 (.in(B), .out(negator_1_out));
  Multiplexer #(.width(8)) multiplexer_1 (.in0(negator_1_out), .in1(B), .out(multiplexer_1_out), .sel(opcode[0]));
  Adder adder_1 (.a(A), .b(multiplexer_1_out), .out(adder_1_out), .cin(1'b0), .cout(adder_1_cout));
  LED led_1 (.in(adder_1_cout));
  or or_1 (or_1_out, A[7], A[6], A[5], A[4], A[3], A[2], A[1], A[0]);
  assign and_1_out = A & B;  // AND_Gate and_1, 8 bits wide
  assign or_2_out = A | B;  // OR_Gate or_2, 8 bits wide
  assign not_1_out = ~B;  // NOT_Gate not_1, 8 bits wide
  Shifter shifter_1 (.in(A), .\dist (B[2:0]), .out(shifter_1_out));
  Shifter #(.shift("lr")) shifter_2 (.in(A), .\dist (B[2:0]), .out(shifter_2_out));
  assign bit_extender_1_out = {{7{1'b0}}, or_1_out};  // Bit_Extender bit_extender_1
  Multiplexer #(.select(4), .width(8)) multiplexer_2 (
    .in0(bit_extender_1_out), .in1(bit_extender_1_out), .in2(B), .in3(B), .in4(B), .in5(B), .in6(B),
    .in7({B[3:0], A[3:0]}), .in8({A[7:4], B[3:0]}), .in9(adder_1_out), .in10(adder_1_out), .in11(and_1_out),
    .in12(or_2_out), .in13(not_1_out), .in14(shifter_1_out), .in15(shifter_2_out), .out(R), .sel(opcode));
endmodule

module PIPE_EXMD (
  input  [7:0] DA_in,
  input  Branch_in,
  input  [7:0] Res_in,
  input  Load_in,
  input  RWE_in,
  input  MWE_in,
  input  [7:0] PC_in,
  input  [1:0] RD_in,
  input  R,
  input  Clk,
  output [7:0] DA_out,
  output Branch_out,
  output [7:0] Res_out,
  output Load_out,
  output RWE_out,
  output MWE_out,
  output [7:0] PC_out,
  output [1:0] RD_out
);

  wire multiplexer_1_out, multiplexer_2_out, multiplexer_3_out;

  Register DA (.D(DA_in), .en(1'b1), .clk(Clk), .Q(DA_out), .clr(1'b0));
  Register #(.width(1)) Branch (.D(multiplexer_1_out), .en(1'b1), .clk(Clk), .Q(Branch_out), .clr(1'b0));
  Multiplexer multiplexer_1 (.in0(Branch_in), .in1(1'b0), .out(multiplexer_1_out), .sel(R));
  Register Res (.D(Res_in), .en(1'b1), .clk(Clk), .Q(Res_out), .clr(1'b0));
  Register #(.width(1)) Load (.D(Load_in), .en(1'b1), .clk(Clk), .Q(Load_out), .clr(1'b0));
  Register #(.width(1)) RWE (.D(multiplexer_2_out), .en(1'b1), .clk(Clk), .Q(RWE_out), .clr(1'b0));
  Multiplexer multiplexer_2 (.in0(RWE_in), .in1(1'b0), .out(multiplexer_2_out), .sel(R));
  Register #(.width(1)) MWE (.D(multiplexer_3_out), .en(1'b1), .clk(Clk), .Q(MWE_out), .clr(1'b0));
  Multiplexer multiplexer_3 (.in0(MWE_in), .in1(1'b0), .out(multiplexer_3_out), .sel(R));
  Register PC (.D(PC_in), .en(1'b1), .clk(Clk), .Q(PC_out), .clr(1'b0));
  Register #(.width(2)) RD (.D(RD_in), .en(1'b1), .clk(Clk), .Q(RD_out), .clr(1'b0));
endmodule

module PIPE_MDWB (
  input  [7:0] Res_in,
  input  [7:0] Mem_in,
  input  Load_in,
  input  [1:0] RD_in,
  input  WE_in,
  input  Clk,
  input  R,
  output [7:0] Res_out,
  output [7:0] Mem_out,
  output Load_out,
  output [1:0] RD_out,
  output WE_out
);

  wire multiplexer_1_out;

  Register Res (.D(Res_in), .en(1'b1), .clk(Clk), .Q(Res_out), .clr(1'b0));
  Register Mem (.D(Mem_in), .en(1'b1), .clk(Clk), .Q(Mem_out), .clr(1'b0));
  Register #(.width(1)) Load (.D(Load_in), .en(1'b1), .clk(Clk), .Q(Load_out), .clr(1'b0));
  Register #(.width(2)) RD (.D(RD_in), .en(1'b1), .clk(Clk), .Q(RD_out), .clr(1'b0));
  Register #(.width(1)) WE (.D(multiplexer_1_out), .en(1'b1), .clk(Clk), .Q(WE_out), .clr(1'b0));
  Multiplexer multiplexer_1 (.in0(WE_in), .in1(1'b0), .out(multiplexer_1_out), .sel(R));
endmodule
